# Fritzing sketch Feather (saved by Fritzing 0.9.3b)
breadboards: 1

parts:
  Part1 = Adafruit Feather HUZZAH ESP8266 [part_number="Adafruit #2821"]
  Part2 = Adafruit OLED FeatherWing [part_number="Adafruit #2900"]
  DHT1 = DHT22 Humidity and Temperature Sensor
  DS1 = DS18B20 1-Wire Temperature Sensor [part_number=DS18B20]  # not connected
  Part3 = Adafruit GPS FeatherWing [part_number="Adafruit #3133"]
  Part4 = Adafruit Feather 32u4 FONA [part_number="Adafruit #3027"]  # not connected
  PIR1 = PIR sensor  # not connected
  U1 = SM130 [package=sm130]  # not connected
  R1 = Resistor [tolerance=±5% resistance=4.7k package=THT]
  Part5 = MicroSD Card Module  # not connected
  microSD1 = MicroSD Breakout  # not connected
  microSD_Transflash1 = SparkFun - microSD Transflash  # not connected

nets:
  N1: Part1.TXD, Part3.TX
  N2: Part1.RXD, Part3.RX
  GND: Part1.GND, DHT1.GND
  3.3V: Part1.3.3V, DHT1.VDD, R1.Pin_1
  N3: Part1.GPIO15, DHT1.DATA, R1.Pin_0
  N4: Part1.GPIO0, Part2.J
  N5: Part1.GPIO16, Part2.I
  N6: Part1.GPIO2, Part2.H
  N7: Part1.GPIO5/SCL, Part2.SCL
  N8: Part1.GPIO4/SDA, Part2.SDA

notes:
  read > every 2 sec

custom parts:
  Adafruit Feather HUZZAH ESP8266: his is the Adafruit Feather HUZZAH ESP8266 - our take on an 'all-in-one' ESP8266 WiFi development board with built in USB and battery charging. Its an ESP8266 WiFi module with all the extras you need, ready to rock! We have other boards in the Feather family, check'em out here. At the Feather HUZZAH's heart is an ESP8266 WiFi microcontroller clocked at 80 MHz and at 3.3V logic. This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
  Adafruit OLED FeatherWing: This is the FeatherWing OLED: it adds a 128x32 monochrome OLED plus 3 user buttons to any Feather main board. These displays are small, only about 1" diagonal, but very readable due to the high contrast of an OLED display. This screen is made of 128x32 individual white OLED pixels and because the display makes its own light, no backlight is required. This reduces the power required to run the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
  Adafruit GPS FeatherWing: Give your Feather a sense of place, with an Ultimate GPS FeatherWing. In 2013 we designed the Ultimate GPS module to satisfy all your GPS desires - and now we have brought its power and versatility plus more to our Feather series with the Adafruit Ultimate GPS FeatherWing! This FeatherWing plugs right into your Feather board and gives it a precise, sensitive, and low power GPS module for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
  Adafruit Feather 32u4 FONA: This is the Adafruit Feather 32u4 FONA - our take on an 'all-in-one' Arduino-compatible + audio/sms/data capable cellular with built in USB and battery charging. Its an Adafruit Feather 32u4 with a FONA800 module, ready to rock! We have other boards and accessories in the Feather family, check'em out here. At the Feather 32u4's heart is at ATmega32u4 clocked at 8 MHz and at 3.3V logic, a chip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
  MicroSD Breakout: 5V-ready microSD Breakout with Level Shifter
